# Fritzing sketch sleepypico (saved by Fritzing 0.9.3b)
breadboards: 1

parts:
  Mod1 = Raspberry Pi Pico
  S1 = Momentary Switch [package=ksa_sealed_tac_switch]
  Bauteil1 = BME280 Breakout
  Grove1 = Grove OLED 128x96

nets:
  N1: Mod1.pin_3, Mod1.pin_8, Mod1.pin_13, Mod1.pin_18, Mod1.pin_23, Mod1.pin_28, Mod1.pin_33, Mod1.pin_38
  N2: Mod1.pin_20, S1.4
  N3: Mod1.pin_21, Bauteil1.SDO/ADR
  N4: Mod1.pin_22, Bauteil1.!CS
  N5: Mod1.pin_24, Bauteil1.SCK/SCL
  N6: Mod1.pin_25, Bauteil1.SDI/SDA
  GND: Mod1.pin_27, Bauteil1.GND, Grove1.GND
  N7: Mod1.pin_34, Grove1.SCL
  N8: Mod1.pin_35, Grove1.SDA
  3.3V: Mod1.pin_36, S1.1, Bauteil1.3.3V, Grove1.VCC

custom parts:
  Raspberry Pi Pico: Raspberry Pi Pico. Based around the RP2040 microcontroller the Pico is a low cost microcontroller device bringing Raspberry Pi quality, cost, and easy of use to the microcontroller space. Jan 2021, Split part in to two versions: tht (this one) and SMD. This one will drill holes for a .1 in header in pcb to allow plugging in the module as well as providing pads to solder the module to the top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
